# Fritzing sketch Schematic (saved by Fritzing 0.9.2b)
breadboards: 1

parts:
  part = Arduino Uno (Rev3)
  U1 = QRD1114 [package=qrd1114]
  part_2 = QRD1114 [package=qrd1114]
  RSense = Resistor [tolerance=±5% resistance=50k package=THT]
  part_3 = Resistor [tolerance=±5% resistance=200 package=THT]
  part_4 = Resistor [tolerance=±5% resistance=200 package=THT]
  RSense_2 = Resistor [tolerance=±5% resistance=50k package=THT]

nets:
  N1: part.GND, U1.C, U1.K, part_2.C, part_2.K
  N2: part.5V, RSense.Pin_0, part_3.Pin_0, part_4.Pin_0, RSense_2.Pin_0
  N3: U1.E, RSense_2.Pin_1
  N4: U1.A, part_4.Pin_1
  N5: part_2.E, RSense.Pin_1
  N6: part_2.A, part_3.Pin_1
